# Fritzing sketch ManejarMotores (saved by Fritzing 0.9.3b)
breadboards: 1

parts:
  Pololu_A1 = Pololu A4988 [package=SO16]
  C1 = Capacitor Polarized [package=panasonic_c]
  M1 = Stepper Motor - Bipolar
  Componente1 = Arduino Mega 2560 (Rev3)
  IR1 = TSOP312.., 314.. [package=THT]
  J1 = Basic Servo
  M2 = DC Motor  # not connected
  Componente2 = Motor Driver 1A Dual TB6612FNG
  Power_plug1 = Power plug

nets:
  N1: Pololu_A1.RESET, Pololu_A1.SLEEP
  N2: Pololu_A1.STEP, Componente1.D9_PWM
  N3: Pololu_A1.DIR, Componente1.D13_PWM
  GND: Pololu_A1.GND#8, IR1.GND, J1.gnd, Componente2.GND
  VDD: Pololu_A1.VDD, IR1.Vs, J1.vcc, Componente2.PWMA
  N4: Pololu_A1.1B, M1.D
  N5: Pololu_A1.1A, M1.B
  N6: Pololu_A1.2A, M1.C
  N7: Pololu_A1.2B, M1.A
  N8: Pololu_A1.GND#14, C1.-, Power_plug1.GND
  N9: Pololu_A1.VMOT, C1.+, Power_plug1.VCC
  N10: Componente1.D11_PWM, IR1.Data
  N11: Componente1.D6_PWM, J1.pulse
  N12: Componente1.D52, Componente2.AIN2
  N13: Componente1.D53, Componente2.AIN1
