# Fritzing sketch Medidor (saved by Fritzing 0.9.3b)
breadboards: 1

parts:
  R1 = Resistor [tolerance=±5% resistance=10k package=THT]
  R2 = Resistor [tolerance=±5% resistance=10k package=THT]
  C1 = Electrolytic Capacitor [capacitance=10µF package="100 mil [THT, electrolytic]"]
  R3 = Resistor [tolerance=±5% resistance=33 package=THT]
  Componente1 = Arduino Uno (Rev3)
  U1 = Transformer [package=transformer]
  V1 = AC Power [voltage=110 frequency=60]

nets:
  N1: R1.Pin_0, R2.Pin_1, C1.+, R3.Pin_1, U1.3
  N2: R1.Pin_1, Componente1.5V
  N3: R2.Pin_0, C1.-, Componente1.GND
  N4: R3.Pin_0, Componente1.A1, U1.4
  N5: U1.1, V1.V+
  N6: U1.2, V1.V-

notes:
  SensorCorriente
