# Fritzing sketch Untitled Sketch (saved by Fritzing 0.9.3b)
breadboards: 1

parts:
  Componente1 = SparkFun ESP8266 Thing
  D1 = Rectifier Diode [part_number=1N4001 package="300 mil [THT]"]
  R1 = Resistor [tolerance=±5% resistance=1k package=THT]
  WeMos_D1_Mini_OLED_Shield1 = WeMos D1 Mini OLED Shield
  R2 = Rotary Potentiometer (Small) [maximum_resistance=100kΩ package=THT]

nets:
  VCC: Componente1.VCC, WeMos_D1_Mini_OLED_Shield1.3V3
  N1: Componente1.GPIO2, WeMos_D1_Mini_OLED_Shield1.D1
  N2: Componente1.GPIO14, WeMos_D1_Mini_OLED_Shield1.D2
  N3: Componente1.USBVCC, R1.Pin_0
  N4: Componente1.GND, D1.cathode, WeMos_D1_Mini_OLED_Shield1.G, R2.leg1
  N5: Componente1.GPIO12, WeMos_D1_Mini_OLED_Shield1.RST
  N6: Componente1.ADC, R2.wiper
  N7: D1.anode, R1.Pin_1, R2.leg2
