# Fritzing sketch Domotica_ChatBot (saved by Fritzing 0.9.3b)
breadboards: 1

parts:
  U1 = Module 4 Relais 5V [package="Module 4 Relais 5V"]
  Componente1 = Arduino Uno (Rev3)
  S1 = Pushbutton [package="[THT]"]
  S3 = Pushbutton [package="[THT]"]
  S4 = Pushbutton [package="[THT]"]

nets:
  VCC: U1.VCC, Componente1.5V
  GND: U1.GND, Componente1.GND, S1.Pin_3, S1.Pin_4, S3.Pin_3, S3.Pin_4, S4.Pin_3, S4.Pin_4
  N1: U1.IN1, Componente1.D6_PWM
  N2: U1.IN2, Componente1.D5_PWM
  N3: U1.IN3, Componente1.D4
  N4: Componente1.D10_PWM/SS, S4.Pin_1, S4.Pin_2
  N5: Componente1.D11_PWM/MOSI, S1.Pin_1, S1.Pin_2
  N6: Componente1.D12/MISO, S3.Pin_1, S3.Pin_2

custom parts:
  Module 4 Relais 5V: Module 4 Relais 5V 4x SPD-06VDC-SD-C
