# Fritzing sketch Corazon (saved by Fritzing 0.9.3b)
breadboards: 1

parts:
  Componente1 = Arduino Uno (Rev3) [part_number="Arduino Uno"]
  J2 = female pin header, 6 pins [form="♀ (female)" part_number=HC-05]
  VCC1 = 4 x AAA Battery Mount
  J1 = single row smd female pin header, 6 pins [form="♀ (female)" part_number="Sensor Corazon"]

nets:
  A3: Componente1.A3, J1.pin3
  D2: Componente1.D2, J2.pin4
  D3: Componente1.D3_PWM, J2.pin5
  D4: Componente1.D4, J1.pin4
  D5: Componente1.D5_PWM, J1.pin5
  3.3V: Componente1.3V3, J1.pin2
  5V: Componente1.5V, J2.pin2
  GND: Componente1.GND, J2.pin3, VCC1.-, J1.pin1
  Vin: Componente1.VIN, VCC1.+

notes:
  Key
  5vc
  GND
  TXD
  RXD
  Sate
  Hc-05
  AD8232
  3.3V
  OUTPUT
  LO-
  LO+
  SDN
  conecciones basicas para hacer
  un electrocardiograma con arduino
  mas infor en alsw.net
  ElectroCardiograma Bluetoth, Creado por Chepecarlos, sistema para medir ritmo cardiaco por Bluettoth
