# Fritzing sketch Diagrama (saved by Fritzing 0.9.3b)
breadboards: 1

parts:
  J2 = female pin header, 20 pins [form="♀ (female)"]
  J3 = female pin header, 20 pins [form="♀ (female)"]
  microSD_Transflash1 = SparkFun - microSD Transflash

nets:
  N1: J2.pin4, microSD_Transflash1.GND
  N2: J2.pin5, microSD_Transflash1.VCC
  N3: J3.pin10, microSD_Transflash1.CD
  N4: J3.pin13, microSD_Transflash1.SCK
  N5: J3.pin14, microSD_Transflash1.DO
  N6: J3.pin15, microSD_Transflash1.DI
