# Fritzing sketch LectorBuella (saved by Fritzing 0.9.3b)
circuit board: 7.50404cm x 7.9952cm
breadboards: 1

parts:
  Componente1 = Arduino Uno (Rev3) [part_number="Arduino Uno"]
  Componente2 = Logic Level Converter
  R2 = Rotary Potentiometer (Small) [maximum_resistance=100kΩ package=THT]
  J2 = female pin header, 4 pins [form="♀ (female)"]
  J3 = Piezo Speaker [part_number=Buzzer]
  R3 = Rotary Potentiometer (Small) [maximum_resistance=100kΩ package=THT]
  U1 = LCD-16X2 [part_number=LCD package=lcd-16x2_noholes]
  J1 = rounded female pin header, 2 pins [form="♀ (female rounded)" part_number="Escudo Wifi"]  # not connected

nets (from the pcb view):
  N1: Componente1.A0, Componente2.TX2_HV
  N2: Componente1.A1, Componente2.RX2_HV
  N3: Componente1.A2, J3.pin2
  N4: Componente1.D11_PWM/MOSI, U1.E
  N5: Componente1.D12/MISO, U1.RS
  GND: Componente1.GND, Componente2.GND, J2.pin3, J3.pin1, R3.leg2, U1.R_W, U1.K
  N6: Componente1.D2, U1.DB7
  N7: Componente1.D3_PWM, U1.DB6
  N8: Componente1.D4, U1.DB5
  N9: Componente1.D5_PWM, U1.DB4
  N10: Componente1.3V3, Componente2.LV, J2.pin4
  5V: Componente1.5V, Componente2.HV, R2.leg1, R3.leg1, U1.VDD
  N11: Componente2.TX2_LV, J2.pin1
  N12: Componente2.RX2_LV, J2.pin2
  N13: R2.wiper, U1.VO
  N14: R2.leg2, U1.VSS
  N15: R3.wiper, U1.A

notes:
  Escudo ESP8266
  Sensor Biometrico
  TX
  RX
  GND
  VCC
  Buzzer
  Sistema de Ingreso, Creado por Chepecarlos: Proyecto para saber a que hora llegan y salen los minion, 1.0
