# Fritzing sketch Diseño (saved by Fritzing 0.9.3b)
breadboards: 1

parts:
  Componente1 = Arduino ProtoShield
  J2 = female pin header, 8 pins [form="♀ (female)"]
  Power_plug1 = Power plug
  J1 = female pin header, 4 pins [form="♀ (female)"]

nets:
  VIN: Componente1.VIN, Power_plug1.VCC
  N1: Componente1.D3, Componente1.N$28, J2.pin2
  N2: Componente1.D5, Componente1.N$27, J2.pin3
  N3: Componente1.D6, Componente1.N$26, J2.pin4
  N4: Componente1.D7, Componente1.N$25, J2.pin5
  N5: Componente1.A5, Componente1.N$54, J1.pin3
  N6: Componente1.A4, Componente1.N$65, J1.pin2
  N7: Componente1.D8, Componente1.N$24, J2.pin6
  N8: Componente1.D9, Componente1.N$23, J2.pin7
  N9: Componente1.5V, Componente1.N$19, Componente1.N$43, J2.pin1, J1.pin4
  GND: Componente1.GND, Componente1.N$22, Componente1.N$76, J2.pin8, Power_plug1.GND, J1.pin1
