# Fritzing sketch Seguridad (saved by Fritzing 0.9.3b)
breadboards: 1

parts:
  Componente1 = Arduino Uno (Rev3) - ICSP
  S1 = Pushbutton [package="[THT]"]
  R1 = Resistor [tolerance=±5% resistance=10k package=THT]
  J1 = female pin header, 3 pins [form="♀ (female)"]

nets:
  N1: Componente1.D2, J1.pin2
  N2: Componente1.D3_PWM, S1.Pin_1, S1.Pin_2, R1.Pin_1
  N3: Componente1.5V, S1.Pin_3, S1.Pin_4, J1.pin3
  N4: Componente1.GND, R1.Pin_0, J1.pin1

notes:
  GND
  OUT
  Vcc
  Sensor PIR
